// Logisim project 1 bit alu.circ as structural Verilog
// ALU
module _1_bit_artimatic_unint (
  input  B,
  input  A,
  input  Carry_in,
  input  operation,
  input  inverter,
  output Result,
  output Carry_out
);

  wire adder_1_out, and_1_out, multiplexer_1_out, not_1_out;

  not not_1 (not_1_out, B);
  Multiplexer multiplexer_1 (.in0(not_1_out), .in1(B), .out(multiplexer_1_out), .sel(inverter));  // open: en
  and and_1 (and_1_out, B, A);
  Adder #(.width(1)) adder_1 (.a(A), .b(multiplexer_1_out), .out(adder_1_out), .cin(Carry_in), .cout(Carry_out));
  Multiplexer multiplexer_2 (.in0(and_1_out), .in1(adder_1_out), .out(Result), .sel(operation));  // open: en
endmodule

module _8_bit_ALU (
  input  Carry_in,
  input  [7:0] A,
  input  Inverter,
  input  Operation,
  input  [7:0] B,
  output [7:0] out_6,
  output Carry_Out
);

  wire n1_bit_artimatic_unint_1_carry_out, n1_bit_artimatic_unint_2_carry_out,
       n1_bit_artimatic_unint_3_carry_out, n1_bit_artimatic_unint_4_carry_out,
       n1_bit_artimatic_unint_6_carry_out, n1_bit_artimatic_unint_7_carry_out,
       n1_bit_artimatic_unint_8_carry_out;

  _1_bit_artimatic_unint u_1_bit_artimatic_unint_1 (
    .Result(out_6[0]), .B(B[0]), .A(A[0]), .Carry_in(Carry_in), .inverter(Inverter),
    .Carry_out(n1_bit_artimatic_unint_1_carry_out), .operation(Operation));
  _1_bit_artimatic_unint u_1_bit_artimatic_unint_2 (
    .Result(out_6[1]), .B(B[1]), .A(A[1]), .Carry_in(n1_bit_artimatic_unint_1_carry_out),
    .inverter(Inverter), .Carry_out(n1_bit_artimatic_unint_2_carry_out), .operation(Operation));
  _1_bit_artimatic_unint u_1_bit_artimatic_unint_3 (
    .Result(out_6[2]), .B(B[2]), .A(A[2]), .Carry_in(n1_bit_artimatic_unint_2_carry_out),
    .inverter(Inverter), .Carry_out(n1_bit_artimatic_unint_3_carry_out), .operation(Operation));
  _1_bit_artimatic_unint u_1_bit_artimatic_unint_4 (
    .Result(out_6[3]), .B(B[3]), .A(A[3]), .Carry_in(n1_bit_artimatic_unint_3_carry_out),
    .inverter(Inverter), .Carry_out(n1_bit_artimatic_unint_4_carry_out), .operation(Operation));
  _1_bit_artimatic_unint u_1_bit_artimatic_unint_5 (
    .Result(out_6[4]), .B(B[4]), .A(A[4]), .Carry_in(n1_bit_artimatic_unint_4_carry_out),
    .inverter(Inverter), .Carry_out(out_6[1]), .operation(Operation));
  _1_bit_artimatic_unint u_1_bit_artimatic_unint_6 (
    .Result(out_6[5]), .B(B[5]), .A(A[5]), .Carry_in(out_6[1]), .inverter(Inverter),
    .Carry_out(n1_bit_artimatic_unint_6_carry_out), .operation(Operation));
  _1_bit_artimatic_unint u_1_bit_artimatic_unint_7 (
    .Result(out_6[6]), .B(B[6]), .A(A[6]), .Carry_in(n1_bit_artimatic_unint_6_carry_out),
    .inverter(Inverter), .Carry_out(n1_bit_artimatic_unint_7_carry_out), .operation(Operation));
  _1_bit_artimatic_unint u_1_bit_artimatic_unint_8 (
    .Result(out_6[7]), .B(B[7]), .A(A[7]), .Carry_in(n1_bit_artimatic_unint_7_carry_out),
    .inverter(Inverter), .Carry_out(n1_bit_artimatic_unint_8_carry_out), .operation(Operation));
endmodule
