// Logisim project cpu.circ as structural Verilog
module CPU (
  output out_1
);

  wire ADD, AND, and_1_out, and_16_out, and_17_out, and_18_out, and_19_out, Artimatic, clk, Conditional_BRZ,
       controlled_buffer_9_out, EN_ALU, LOAD, MOVI, movi_Imediate, n8_bit_alu_1_zero_flag, not_1_out,
       Operation, or_1_out, or_2_out, OUT, Rd, Sel_A, Sel_B, SHIFT, STOR, SUB, Unconditional_BRZ;
  wire [7:0] A_in, A_out, adder_1_out, Addrese, B_in, B_out, controlled_buffer_1_out,
       controlled_buffer_2_out, controlled_buffer_3_out, controlled_buffer_4_out, controlled_buffer_6_out,
       controlled_buffer_7_out, controlled_buffer_8_out, controlled_buffer_10_out, controlled_buffer_11_out,
       controlled_buffer_12_out, controlled_buffer_13_out, demultiplexer_1_out0, demultiplexer_1_out1,
       multiplexer_1_out, multiplexer_2_out, multiplexer_3_out, multiplexer_4_out, multiplexer_5_out,
       ram_1_data, register_1_q, Result, shifter_1_out_2;
  wire [11:0] ram_2_data;
  wire [11:9] register_3_q;

  assign controlled_buffer_1_out = or_1_out ? Addrese : 8'bz;  // Controlled_Buffer controlled_buffer_1
  or or_1 (or_1_out, LOAD, STOR);
  Clock clock_1 (.out(clk));
  Adder adder_1 (.a(register_1_q), .b(8'h1), .out(adder_1_out));  // open: cin, cout
  RAM #(.bus("separate")) ram_1 (
    .addr(controlled_buffer_1_out), .din(controlled_buffer_2_out), .data(ram_1_data), .str(STOR), .clk(clk),
    .ld(LOAD));  // open: sel, clr
  or or_2 (or_2_out, Unconditional_BRZ, and_1_out);
  Multiplexer #(.width(8)) multiplexer_1 (
    .in0(adder_1_out), .in1(Addrese), .out(multiplexer_1_out), .sel(or_2_out));  // open: en
  and and_1 (and_1_out, out_1, Conditional_BRZ);
  assign controlled_buffer_2_out = STOR ? A_out : 8'bz;  // Controlled_Buffer controlled_buffer_2
  assign controlled_buffer_3_out = LOAD ? ram_1_data : 8'bz;  // Controlled_Buffer controlled_buffer_3
  Demultiplexer #(.width(8)) demultiplexer_1 (
    .out0(demultiplexer_1_out0), .out1(demultiplexer_1_out1), .in(Result), .sel(Rd));  // open: en
  Register register_1 (.D(multiplexer_1_out), .Q(register_1_q), .clk(clk));  // open: en, clr
  assign controlled_buffer_4_out = EN_ALU ? demultiplexer_1_out0 : 8'bz;  // Controlled_Buffer controlled_buffer_4
  assign B_in = EN_ALU ? demultiplexer_1_out1 : 8'bz;  // Controlled_Buffer controlled_buffer_5
  Multiplexer #(.width(8)) multiplexer_2 (
    .in0(controlled_buffer_3_out), .in1(controlled_buffer_4_out), .out(multiplexer_2_out), .sel(EN_ALU));  // open: en
  RAM #(.dataWidth(12)) ram_2 (.addr(register_1_q), .data(ram_2_data), .clk(clk));  // open: sel, ld, clr
  Multiplexer #(.width(8)) multiplexer_3 (
    .in0(multiplexer_2_out), .in1(A_in), .out(multiplexer_3_out), .sel(Sel_A));  // open: en
  assign controlled_buffer_6_out = MOVI ? A_out : 8'bz;  // Controlled_Buffer controlled_buffer_6
  Register register_2 (.D(multiplexer_3_out), .Q(A_out), .clk(clk));  // open: en, clr
  Multiplexer #(.width(8)) multiplexer_4 (
    .in0(controlled_buffer_6_out), .in1(B_in), .out(multiplexer_4_out), .sel(Sel_B));  // open: en
  Register #(.width(12)) register_3 (.D(ram_2_data), .Q({register_3_q, Rd, Addrese}), .clk(clk));  // open: en, clr
  Register #(.trigger("falling")) register_4 (.D(multiplexer_4_out), .Q(B_out), .clk(clk));  // open: en, clr
  assign controlled_buffer_7_out = EN_ALU ? A_out : 8'bz;  // Controlled_Buffer controlled_buffer_7
  assign controlled_buffer_8_out = EN_ALU ? B_out : 8'bz;  // Controlled_Buffer controlled_buffer_8
  and and_2 (movi_Imediate, ~register_3_q[11], ~register_3_q[10], ~register_3_q[9]);  // AND_Gate
  and and_3 (MOVI, ~register_3_q[11], ~register_3_q[10], register_3_q[9]);  // AND_Gate
  and and_4 (LOAD, ~register_3_q[11], register_3_q[10], ~register_3_q[9]);  // AND_Gate
  and and_5 (STOR, ~register_3_q[11], register_3_q[10], register_3_q[9]);  // AND_Gate
  and and_6 (Artimatic, register_3_q[11], ~register_3_q[10], ~register_3_q[9]);  // AND_Gate
  and and_7 (Conditional_BRZ, register_3_q[11], ~register_3_q[10], register_3_q[9]);  // AND_Gate
  and and_8 (Unconditional_BRZ, register_3_q[11], register_3_q[10], ~register_3_q[9]);  // AND_Gate
  and and_9 (OUT, register_3_q[9], register_3_q[10], register_3_q[11]);
  _8_bit_ALU u_8_bit_alu_1 (
    .A(controlled_buffer_7_out), .Inverter(not_1_out), .Operation(Operation), .B(controlled_buffer_8_out),
    .Result(Result), .Carry_in(Addrese[5]), .Zero_flag(n8_bit_alu_1_zero_flag));  // open: Carry_Out
  not not_1 (not_1_out, Addrese[5]);
  Multiplexer #(.width(8)) multiplexer_5 (.in0(A_out), .in1(B_out), .out(multiplexer_5_out), .sel(Rd));  // open: en
  and and_10 (Operation, ~Addrese[7], ~Addrese[6]);  // AND_Gate
  and and_11 (ADD, Artimatic, ~Addrese[5], ~Addrese[6], ~Addrese[7]);  // AND_Gate
  and and_12 (SUB, Addrese[5], Artimatic, ~Addrese[6], ~Addrese[7]);  // AND_Gate
  and and_13 (SHIFT, Addrese[6], ~Addrese[7], Artimatic, ~Addrese[5]);  // AND_Gate
  and and_14 (AND, Addrese[6], Addrese[5], Artimatic, ~Addrese[7]);  // AND_Gate
  assign controlled_buffer_9_out = EN_ALU ? n8_bit_alu_1_zero_flag : 1'bz;  // Controlled_Buffer controlled_buffer_9
  assign controlled_buffer_10_out = SHIFT ? multiplexer_5_out : 8'bz;  // Controlled_Buffer controlled_buffer_10
  Register #(.width(1)) register_5 (.D(controlled_buffer_9_out), .Q(out_1), .clk(clk));  // open: en, clr
  shifter shifter_1 (.in_1(controlled_buffer_10_out), .out_2(shifter_1_out_2));
  Demultiplexer #(.width(8)) demultiplexer_2 (
    .out0(A_in), .out1(B_in), .in(controlled_buffer_11_out), .sel(Rd));  // open: en
  assign controlled_buffer_11_out = SHIFT ? shifter_1_out_2 : 8'bz;  // Controlled_Buffer controlled_buffer_11
  assign controlled_buffer_12_out = OUT ? A_out : 8'bz;  // Controlled_Buffer controlled_buffer_12
  assign controlled_buffer_13_out = movi_Imediate ? Addrese : 8'bz;  // Controlled_Buffer controlled_buffer_13
  and and_15 (EN_ALU, ~SHIFT, Artimatic);  // AND_Gate
  Register register_6 (.D(controlled_buffer_12_out), .clk(clk));  // open: en, Q, clr
  Demultiplexer #(.width(8)) demultiplexer_3 (
    .out0(A_in), .out1(B_in), .in(controlled_buffer_13_out), .sel(Rd));  // open: en
  and and_16 (and_16_out, ~Rd, SHIFT);  // AND_Gate
  and and_17 (and_17_out, ~Rd, movi_Imediate);  // AND_Gate
  and and_18 (and_18_out, Rd, Artimatic);
  and and_19 (and_19_out, movi_Imediate, Rd);
  or or_3 (Sel_B, and_18_out, and_19_out);
  or or_4 (Sel_A, and_16_out, and_17_out);

  // Other names for the same wires on the sheet: Data[7:0] = Addrese; carry_in = Addrese[5]; Zero_Flag = out_1

  // Notes on the sheet:
  //   System Clock
  //      Data Memory 
  //   Sequntale excute incremet PC
  //                         Program Counter
  //                                                              Instruction Memory 
  //                         Instruciton Regester
  //       A
  //   Instruction Decoder 
  //   B
  //                            Hardwired Control Unit 
  //   Shift Operation
  //   selector for MUX
  //   implementation of OUT  instruction
  //   implement the imdiate move instructioln
  //   Selector for Registor A
  //   Selector for Registor B
  //   IBR
endmodule

// ALU
module _1_bit_artimatic_unint (
  input  B,
  input  A,
  input  Carry_in,
  input  operation,
  input  inverter,
  output Result,
  output Carry_out
);

  wire adder_1_out, and_1_out, multiplexer_1_out, not_1_out;

  not not_1 (not_1_out, B);
  Multiplexer multiplexer_1 (.in0(not_1_out), .in1(B), .out(multiplexer_1_out), .sel(inverter));  // open: en
  and and_1 (and_1_out, B, A);
  Adder #(.width(1)) adder_1 (.a(A), .b(multiplexer_1_out), .out(adder_1_out), .cin(Carry_in), .cout(Carry_out));
  Multiplexer multiplexer_2 (.in0(and_1_out), .in1(adder_1_out), .out(Result), .sel(operation));  // open: en
endmodule

// ALU
module _8_bit_ALU (
  input  Carry_in,
  input  [7:0] A,
  input  Inverter,
  input  Operation,
  input  [7:0] B,
  output [7:0] Result,
  output Zero_flag,
  output Carry_Out
);

  wire n1_bit_artimatic_unint_1_carry_out, n1_bit_artimatic_unint_2_carry_out,
       n1_bit_artimatic_unint_3_carry_out, n1_bit_artimatic_unint_4_carry_out,
       n1_bit_artimatic_unint_6_carry_out, n1_bit_artimatic_unint_7_carry_out,
       n1_bit_artimatic_unint_8_carry_out;

  _1_bit_artimatic_unint u_1_bit_artimatic_unint_1 (
    .Result(Result[0]), .B(B[0]), .A(A[0]), .Carry_in(Carry_in), .inverter(Inverter),
    .Carry_out(n1_bit_artimatic_unint_1_carry_out), .operation(Operation));
  _1_bit_artimatic_unint u_1_bit_artimatic_unint_2 (
    .Result(Result[1]), .B(B[1]), .A(A[1]), .Carry_in(n1_bit_artimatic_unint_1_carry_out),
    .inverter(Inverter), .Carry_out(n1_bit_artimatic_unint_2_carry_out), .operation(Operation));
  _1_bit_artimatic_unint u_1_bit_artimatic_unint_3 (
    .Result(Result[2]), .B(B[2]), .A(A[2]), .Carry_in(n1_bit_artimatic_unint_2_carry_out),
    .inverter(Inverter), .Carry_out(n1_bit_artimatic_unint_3_carry_out), .operation(Operation));
  _1_bit_artimatic_unint u_1_bit_artimatic_unint_4 (
    .Result(Result[3]), .B(B[3]), .A(A[3]), .Carry_in(n1_bit_artimatic_unint_3_carry_out),
    .inverter(Inverter), .Carry_out(n1_bit_artimatic_unint_4_carry_out), .operation(Operation));
  _1_bit_artimatic_unint u_1_bit_artimatic_unint_5 (
    .Result(Result[4]), .B(B[4]), .A(A[4]), .Carry_in(n1_bit_artimatic_unint_4_carry_out),
    .inverter(Inverter), .Carry_out(Result[1]), .operation(Operation));
  _1_bit_artimatic_unint u_1_bit_artimatic_unint_6 (
    .Result(Result[5]), .B(B[5]), .A(A[5]), .Carry_in(Result[1]), .inverter(Inverter),
    .Carry_out(n1_bit_artimatic_unint_6_carry_out), .operation(Operation));
  _1_bit_artimatic_unint u_1_bit_artimatic_unint_7 (
    .Result(Result[6]), .B(B[6]), .A(A[6]), .Carry_in(n1_bit_artimatic_unint_6_carry_out),
    .inverter(Inverter), .Carry_out(n1_bit_artimatic_unint_7_carry_out), .operation(Operation));
  _1_bit_artimatic_unint u_1_bit_artimatic_unint_8 (
    .Result(Result[7]), .B(B[7]), .A(A[7]), .Carry_in(n1_bit_artimatic_unint_7_carry_out),
    .inverter(Inverter), .Carry_out(n1_bit_artimatic_unint_8_carry_out), .operation(Operation));
  nor nor_1 (Zero_flag, Result[0], Result[1], Result[2], Result[3], Result[4], Result[5], Result[6], Result[7]);
endmodule

// Shifter
module shifter (
  input  [7:0] in_1,
  output [7:0] out_2
);

  Shifter shifter_1 (.in(in_1), .\dist (3'b001), .out(out_2));
endmodule
